// Logisim project memoryaddresses.circ as structural Verilog: 2 circuits, main circuit main
module main (
  input  in_1,
  input  in_2,
  input  in_3,
  input  in_4,
  input  in_5,
  output out_6,
  output out_7,
  output out_8,
  output out_9
);

  wire _0000_out, _0001_out, _0010_out, _0011_out, button_1_out, button_2_out, nor_1_out, nor_2_out;

  Button button_1 (.out(button_1_out));
  Button button_2 (.out(button_2_out));
  nor nor_1 (nor_1_out, button_1_out, nor_2_out);
  nor nor_2 (nor_2_out, nor_1_out, button_2_out);
  and _0000 (_0000_out, in_1, in_2, in_4, in_5);
  and _0001 (_0001_out, in_1, in_2, in_4, ~in_5);  // AND_Gate
  and _0010 (_0010_out, in_1, in_2, ~in_4, in_5);  // AND_Gate
  and _0011 (_0011_out, in_1, in_2, ~in_4, ~in_5);  // AND_Gate
  LED led_1 (.in(nor_1_out));
  Data_Latch data_latch_1 (.in_1(in_3), .in_2(_0000_out), .out_3(out_6));
  Data_Latch data_latch_2 (.in_1(in_3), .in_2(_0001_out), .out_3(out_7));
  Data_Latch data_latch_3 (.in_1(in_3), .in_2(_0010_out), .out_3(out_8));
  Data_Latch data_latch_4 (.in_1(in_3), .in_2(_0011_out), .out_3(out_9));
endmodule

module Data_Latch (
  input  in_1,
  input  in_2,
  output out_3
);

  wire and_1_out, and_2_out, nor_2_out, not_1_out;

  not not_1 (not_1_out, in_1);
  and and_1 (and_1_out, not_1_out, in_2);
  and and_2 (and_2_out, not_1_out, in_2);
  nor nor_1 (out_3, and_1_out, nor_2_out);
  nor nor_2 (nor_2_out, out_3, and_2_out);
endmodule
